# Fritzing sketch Stoplicht fritzing V1.1 (saved by Fritzing 0.9.3b)
breadboards: 1

parts:
  LED1 = LED - 5mm [color="Red (633nm)" package="5 mm [THT]"]
  R1 = Resistor [tolerance=±5% resistance=220 package=THT]
  LED2 = LED - 5mm [color="Red (633nm)" package="5 mm [THT]"]
  LED3 = LED - 5mm [color="Red (633nm)" package="5 mm [THT]"]
  LED4 = LED - 5mm [color="Red (633nm)" package="5 mm [THT]"]
  R2 = Resistor [tolerance=±5% resistance=220 package=THT]
  R3 = Resistor [tolerance=±5% resistance=220 package=THT]
  R4 = Resistor [tolerance=±5% resistance=220 package=THT]
  Onderdeel1 = Arduino BT
  LED5 = LED - 5mm [color="Red (633nm)" package="5 mm [THT]"]
  LED6 = LED - 5mm [color="Red (633nm)" package="5 mm [THT]"]
  LED7 = LED - 5mm [color="Red (633nm)" package="5 mm [THT]"]
  LED8 = LED - 5mm [color="Red (633nm)" package="5 mm [THT]"]
  R5 = Resistor [tolerance=±5% resistance=220 package=THT]
  R6 = Resistor [tolerance=±5% resistance=220 package=THT]
  R7 = Resistor [tolerance=±5% resistance=220 package=THT]
  R8 = Resistor [tolerance=±5% resistance=220 package=THT]
  LED9 = LED - 5mm [color="Red (633nm)" package="5 mm [THT]"]
  LED10 = LED - 5mm [color="Red (633nm)" package="5 mm [THT]"]
  R9 = Resistor [tolerance=±5% resistance=220 package=THT]
  R10 = Resistor [tolerance=±5% resistance=220 package=THT]
  S1 = Pushbutton [package="[THT]"]
  R11 = Resistor [tolerance=±5% resistance=220 package=THT]
  S2 = Pushbutton [package="[THT]"]
  R12 = Resistor [tolerance=±5% resistance=220 package=THT]

nets:
  N1: LED1.cathode, Onderdeel1.TX/D1
  N2: LED1.anode, R1.Pin_0
  N3: R1.Pin_1, R2.Pin_0, R3.Pin_0, R4.Pin_0, Onderdeel1.GND, R5.Pin_1, R6.Pin_1, R7.Pin_1, R8.Pin_1, R9.Pin_0, R10.Pin_0, R11.Pin_0
  N4: LED2.cathode, R2.Pin_1
  N5: LED2.anode, Onderdeel1.D2
  N6: LED3.cathode, R3.Pin_1
  N7: LED3.anode, Onderdeel1.PWM_D3
  N8: LED4.cathode, R4.Pin_1
  N9: LED4.anode, Onderdeel1.D4
  N10: Onderdeel1.D8, LED8.cathode
  N11: Onderdeel1.PWM_D9, LED7.cathode
  N12: Onderdeel1.SS/PWM_D10, LED6.cathode
  N13: Onderdeel1.MOSI/PWM_D11, LED5.cathode
  N14: Onderdeel1.MISO/D12, LED10.anode
  N15: Onderdeel1.SCK/D13, S1.Pin_3, S1.Pin_4, R11.Pin_1
  N16: Onderdeel1.PWM_D5, LED9.anode
  N17: Onderdeel1.PWM_D6, S2.Pin_1, S2.Pin_2, R12.Pin_0
  N18: Onderdeel1.5V, S1.Pin_1, S1.Pin_2, S2.Pin_3, S2.Pin_4, R12.Pin_1
  N19: LED5.anode, R5.Pin_0
  N20: LED6.anode, R6.Pin_0
  N21: LED7.anode, R7.Pin_0
  N22: LED8.anode, R8.Pin_0
  N23: LED9.cathode, R9.Pin_1
  N24: LED10.cathode, R10.Pin_1
